# Fritzing sketch CircuitFritzing (saved by Fritzing 0.9.3b)

parts:
  Parça1 = Arduino Uno (Rev3)
  SD_card_module1 = SD Card Module
  PCB2 = RTC_DS1302_module
  Parça2 = BMP180 Breakout (GY-68)

nets:
  N1: Parça1.A4/SDA, Parça2.SDA
  N2: Parça1.A5/SCL, Parça2.SCL
  N3: Parça1.D8, PCB2.RST
  N4: Parça1.D10_PWM/SS, SD_card_module1.CS
  N5: Parça1.D11_PWM/MOSI, SD_card_module1.MOSI
  N6: Parça1.D12/MISO, SD_card_module1.MISO
  N7: Parça1.D13/SCK, SD_card_module1.SCK
  GND: Parça1.GND, SD_card_module1.GND, PCB2.GND, Parça2.GND
  N8: Parça1.D6_PWM, PCB2.CLK
  N9: Parça1.D7, PCB2.DAT
  N10: Parça1.ioref, PCB2.VCC
  3V3: Parça1.3V3, Parça2.VCC
  N11: Parça1.5V, SD_card_module1.+5

custom parts:
  SD Card Module: SD Card Module Slot Socket Reader For Arduino ARM MCU
  RTC_DS1302_module: Arduino module DS1302 SPI Real Time Clock
  BMP180 Breakout (GY-68): This is a simple breakout board for the BMP180, a high-precision, low-power barometric pressure sensor made by Bosch Sensortec. The range of measurement is from 300hPa to 1100hPa. The sensor can be supplied with voltage ranging from 1.8V to 3.6V. Operating temperature range is -40 to +85 °C. This particular breakout board (or perhaps the configuration) is produced by Shenzhen Keep Power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
